// Digital circuit 16bitRegister.dig as structural Verilog
module _16bitRegister (
  input  [7:0] iDB,
  input  nLDL,
  input  nLDH,
  input  DIR,
  input  nCEN,
  input  CLK,
  input  nOEL,
  input  nOEH,
  input  CTL_CLK,
  output [15:0] MB,
  output [15:0] val
);

  wire c74191_1_nrc, c74191_2_nrc, c74191_3_nrc;
  wire [3:0] iDB_H, iDB_L;

  c74191 c74191_1 (
    .nPL(nLDL), .nU_D(DIR), .CP(CLK), .nCE(nCEN), .D0(iDB_L[0]), .D1(iDB_L[1]), .D2(iDB_L[2]), .D3(iDB_L[3]),
    .VCC(1'b1), .GND(1'b0), .Q0(val[0]), .Q1(val[1]), .Q2(val[2]), .Q3(val[3]), .nRC(c74191_1_nrc));  // open: TC
  // _74573 _74573_1: pin names not known; wires that end beside it: 1'b0, CTL_CLK, iDB[0], iDB[1], iDB[2], iDB[3], iDB[4], iDB[5], iDB[6], iDB[7], 1'b1, 1'b0, iDB_L[0], iDB_L[1], iDB_L[2], iDB_L[3], iDB_H[0], iDB_H[1], iDB_H[2], iDB_H[3]
  c74191 c74191_2 (
    .nPL(nLDL), .nU_D(DIR), .CP(CLK), .nCE(c74191_1_nrc), .D0(iDB_H[0]), .D1(iDB_H[1]), .D2(iDB_H[2]),
    .D3(iDB_H[3]), .VCC(1'b1), .GND(1'b0), .Q0(val[4]), .Q1(val[5]), .Q2(val[6]), .Q3(val[7]),
    .nRC(c74191_2_nrc));  // open: TC
  c74191 c74191_3 (
    .nPL(nLDH), .nU_D(DIR), .CP(CLK), .nCE(c74191_2_nrc), .D0(iDB_L[0]), .D1(iDB_L[1]), .D2(iDB_L[2]),
    .D3(iDB_L[3]), .VCC(1'b1), .GND(1'b0), .Q0(val[8]), .Q1(val[9]), .Q2(val[10]), .Q3(val[11]),
    .nRC(c74191_3_nrc));  // open: TC
  // _74245 _74245_1: pin names not known; wires that end beside it: 1'b1, 1'b1, 1'b0, val[0], val[1], val[2], val[3], val[4], val[5], val[6], val[7], nOEL, MB[0], MB[1], MB[2], MB[3], MB[4], MB[5], MB[6], MB[7]
  // _74245 _74245_2: pin names not known; wires that end beside it: 1'b1, 1'b1, 1'b0, val[8], val[9], val[10], val[11], val[12], val[13], val[14], val[15], nOEH, MB[8], MB[9], MB[10], MB[11], MB[12], MB[13], MB[14], MB[15]
  c74191 c74191_4 (
    .nPL(nLDH), .nU_D(DIR), .CP(CLK), .nCE(c74191_3_nrc), .D0(iDB_H[0]), .D1(iDB_H[1]), .D2(iDB_H[2]),
    .D3(iDB_H[3]), .VCC(1'b1), .GND(1'b0), .Q0(val[12]), .Q1(val[13]), .Q2(val[14]), .Q3(val[15]));  // open: TC, nRC

  // Other names for the same wires on the sheet: iMB0[3:0] = val[3:0]; iMB1[3:0] = val[7:4]; iMB2[3:0] = val[11:8];
  //   iMB3[3:0] = val[15:12]; OEH = nOEH; OEL = nOEL

  // Notes on the sheet:
  //   nLDL: default 1
  //   nLDH: default 1
  //   nCEN: default 1
  //   Input Pins
  //   LOW Byte
  //   INPUT
  //   HIGH Byte
  //   OUTPUT
endmodule
