// Digital circuit 8bitRegister.dig as structural Verilog
module _8bitRegister (
  input  [7:0] DB,
  input  CLK,
  input  nELHB,
  input  nERHB,
  input  nW,
  output [7:0] RHB,
  output [7:0] LHB,
  output [7:0] val
);

  // _74377 Register: pin names not known; wires that end beside it: 1'b1, 1'b0, DB[0], DB[1], DB[2], DB[3], DB[4], DB[5], DB[6], DB[7], nW, CLK, val[0], val[1], val[2], val[3], val[4], val[5], val[6], val[7]
  // _74245 RHB_OUT: pin names not known; wires that end beside it: 1'b1, 1'b1, 1'b0, val[0], val[1], val[2], val[3], val[4], val[5], val[6], val[7], nERHB, RHB[0], RHB[1], RHB[2], RHB[3], RHB[4], RHB[5], RHB[6], RHB[7]
  // _74245 LHB_OUT: pin names not known; wires that end beside it: 1'b1, 1'b1, 1'b0, val[0], val[1], val[2], val[3], val[4], val[5], val[6], val[7], nELHB, LHB[0], LHB[1], LHB[2], LHB[3], LHB[4], LHB[5], LHB[6], LHB[7]

  // Other names for the same wires on the sheet: ELHB = nELHB; ERHB = nERHB; w = nW
endmodule
