// Digital circuit DataRegisters.dig as structural Verilog
module DataRegisters (
  input  [2:0] D_LBE,
  input  [2:0] D_RBE,
  input  [2:0] D_WE,
  input  [7:0] DB,
  input  CLK,
  output [7:0] LHB,
  output [7:0] RHB,
  output [7:0] X,
  output [7:0] Y,
  output [7:0] A,
  output [7:0] T
);

  wire ELHB_a, ELHB_t, ELHB_x, ELHB_y, ELRB_a, ELRB_t, ELRB_x, ELRB_y, LB_Ctrl_p9, RB_Ctrl_p9, WE_a, WE_t,
       WE_x, WE_Y;

  // _74138 LB_Ctrl: pin names not known; wires that end beside it: 1'b1, 1'b0, 1'b1, 1'b0, 1'b0, D_LBE[0], D_LBE[1], D_LBE[2], LB_Ctrl_p9, ELHB_x, ELHB_y, ELHB_a, ELHB_t, LB_Ctrl_p9
  // _74138 RB_Ctrl: pin names not known; wires that end beside it: 1'b1, 1'b0, 1'b1, 1'b0, 1'b0, D_RBE[0], D_RBE[1], D_RBE[2], RB_Ctrl_p9, ELRB_x, ELRB_y, ELRB_a, ELRB_t, RB_Ctrl_p9
  // _74138 W_Ctrl: pin names not known; wires that end beside it: 1'b1, 1'b0, 1'b1, 1'b0, 1'b0, D_WE[0], D_WE[1], D_WE[2], WE_x, WE_Y, WE_a, WE_t
  _8bitRegister u_X (.DB(DB), .CLK(CLK), .nELHB(ELHB_x), .nERHB(ELRB_x), .nW(WE_x), .RHB(RHB), .LHB(LHB), .val(X));
  _8bitRegister u_Y (.DB(DB), .CLK(CLK), .nELHB(ELHB_y), .nERHB(ELRB_y), .nW(WE_Y), .RHB(RHB), .LHB(LHB), .val(Y));
  _8bitRegister u_A (.DB(DB), .CLK(CLK), .nELHB(ELHB_a), .nERHB(ELRB_a), .nW(WE_a), .RHB(RHB), .LHB(LHB), .val(A));
  _8bitRegister u_T (.DB(DB), .CLK(CLK), .nELHB(ELHB_t), .nERHB(ELRB_t), .nW(WE_t), .RHB(RHB), .LHB(LHB), .val(T));

  // Other names for the same wires on the sheet: dlbe[2:0] = D_LBE; drbe[2:0] = D_RBE; dwe[2:0] = D_WE

  // Notes on the sheet:
  //   ERHB/ELHB/W
  //   000 - OFF
  //   001 - X Register
  //   010 - Y Register
  //   011 - A Register
  //   100 - T Register
endmodule
