// Digital circuit j8ger_cpu.dig as structural Verilog
module j8ger_cpu (
  input  clk
);

  wire d_ff_1_nq, d_ff_1_q, DOWN_out, multiplexer_1_out, RIGHT_out;

  Button RIGHT (.out(RIGHT_out));
  Multiplexer multiplexer_1 (.sel(d_ff_1_q), .in_0(RIGHT_out), .in_1(clk), .out(multiplexer_1_out));
  D_FF d_ff_1 (.D(d_ff_1_nq), .C(DOWN_out), .Q(d_ff_1_q), .nQ(d_ff_1_nq));
  Button DOWN (.out(DOWN_out));
  _8bitRegister X ();  // open: DB, CLK, nELHB, nERHB, nW, RHB, LHB, val
  _8bitRegister Y ();  // open: DB, CLK, nELHB, nERHB, nW, RHB, LHB, val
  _8bitRegister A ();  // open: DB, CLK, nELHB, nERHB, nW, RHB, LHB, val
  _8bitRegister T ();  // open: DB, CLK, nELHB, nERHB, nW, RHB, LHB, val
endmodule
